# Fritzing sketch Word-Clock-RTC-frtizing (saved by Fritzing 0.9.3b)

parts:
  Part1 = Arduino Uno (Rev3)
  Part2 = Adafruit DS3231 [part_number="Adafruit #3013"]

nets:
  N1: Part1.A4/SDA, Part2.SDA
  N2: Part1.A5/SCL, Part2.SCL
  3V3: Part1.3V3, Part2.Vin
  GND: Part1.GND, Part2.GND

notes:
  SDA (Green) - A4
  SCL (Blue) - A5

custom parts:
  Adafruit DS3231: The datasheet for the DS3231 explains that this part is an "Extremely Accurate I²C-Integrated RTC/TCXO/Crystal". And, hey, it does exactly what it says on the tin! This Real Time Clock (RTC) is the most precise you can get in a small, low power package. Most RTCs use an external 32kHz timing crystal that is used to keep time with low current draw. And that's all well and good, but those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
